// Digital circuit part_c.dig as structural Verilog
module part_c (
  input  in_0,
  input  in_1,
  input  in_2,
  output out_0
);

  wire fgnfet_1_d, fgnfet_4_s, pfet_1_d, pfet_3_d, pfet_4_d;

  FGNFET fgnfet_1 (.G(in_2), .D(fgnfet_1_d), .S(1'b1));
  PFET pfet_1 (.G(in_1), .S(1'b0), .D(pfet_1_d));
  PFET pfet_2 (.G(in_2), .S(pfet_1_d), .D(fgnfet_1_d));
  FGNFET fgnfet_2 (.G(in_1), .D(fgnfet_1_d), .S(1'b1));
  PFET pfet_3 (.G(fgnfet_1_d), .S(1'b0), .D(pfet_3_d));
  FGNFET fgnfet_3 (.G(fgnfet_1_d), .D(pfet_3_d), .S(1'b1));
  PFET pfet_4 (.G(in_0), .S(1'b0), .D(pfet_4_d));
  FGNFET fgnfet_4 (.G(in_0), .D(pfet_4_d), .S(fgnfet_4_s));
  FGNFET fgnfet_5 (.G(pfet_3_d), .D(fgnfet_4_s), .S(1'b1));
  PFET pfet_5 (.G(pfet_3_d), .S(1'b0), .D(pfet_4_d));
  PFET pfet_6 (.G(pfet_4_d), .S(1'b0), .D(out_0));
  FGNFET fgnfet_6 (.G(pfet_4_d), .D(out_0), .S(1'b1));
endmodule

/* Test case part_c_test:
in_0 in_1 in_2 out_0
 0    0    0      0
 0    0	   1      0
 0    1    0      0
 0    1    1      0
 1    0    0      0
 1    0    1      1
 1    1    0      1
 1    1    1      1
*/
